// Digital circuit adv-1b.dig as structural Verilog
module adv_1b (
  input  A,
  input  B
);

  wire _7400_1_pin3, _7402_1_pin1, _7404_1_pin2, _7404_1_pin4, _7408_1_pin3, _7432_1_pin3, _7486_1_pin3,
       _747266_1_pin3;

  _7404 _7404_1 (
    .pin1(A), .pin2(_7404_1_pin2), .pin3(B), .pin4(_7404_1_pin4), .pin5(1'b0), .pin7(1'b0), .pin9(1'b0),
    .pin11(1'b0), .pin13(1'b0), .pin14(1'b1));  // open: pin6, pin8, pin10, pin12
  LED NOT_A (.in(_7404_1_pin2));
  LED NOT_B (.in(_7404_1_pin4));
  // PolarityAwareLED polarityawareled_1: pin names not known; wires that end beside it: 1'b1, 1'b1, 1'b1, 1'b1, 1'b1
  _7408 _7408_1 (
    .pin1(A), .pin2(B), .pin3(_7408_1_pin3), .pin4(1'b0), .pin5(1'b0), .pin7(1'b0), .pin8(1'b1), .pin9(1'b1),
    .pin10(1'b1), .pin12(1'b1), .pin13(1'b1), .pin14(1'b1));  // open: pin6, pin11
  _7432 _7432_1 (
    .pin1(A), .pin2(B), .pin3(_7432_1_pin3), .pin4(1'b0), .pin5(1'b0), .pin7(1'b0), .pin8(1'b1), .pin9(1'b1),
    .pin10(1'b1), .pin12(1'b1), .pin13(1'b1), .pin14(1'b1));  // open: pin6, pin11
  _7486 _7486_1 (
    .pin1(A), .pin2(B), .pin3(_7486_1_pin3), .pin4(1'b0), .pin5(1'b0), .pin7(1'b0), .pin9(1'b1),
    .pin10(1'b1), .pin12(1'b1), .pin13(1'b1), .pin14(1'b1));  // open: pin6, pin8, pin11
  LED AND (.in(_7408_1_pin3));
  LED OR (.in(_7432_1_pin3));
  LED XOR (.in(_7486_1_pin3));
  _7400 _7400_1 (
    .pin1(A), .pin2(B), .pin3(_7400_1_pin3), .pin4(1'b0), .pin5(1'b0), .pin7(1'b0), .pin8(1'b1), .pin9(1'b1),
    .pin10(1'b1), .pin12(1'b1), .pin13(1'b1), .pin14(1'b1));  // open: pin6, pin11
  _7402 _7402_1 (
    .pin1(_7402_1_pin1), .pin2(A), .pin3(B), .pin5(1'b0), .pin6(1'b0), .pin7(1'b0), .pin8(1'b1), .pin9(1'b1),
    .pin11(1'b1), .pin12(1'b1), .pin14(1'b1));  // open: pin4, pin10, pin13
  _747266 _747266_1 (
    .pin1(A), .pin2(B), .pin3(_747266_1_pin3), .pin5(1'b0), .pin6(1'b0), .pin7(1'b0), .pin8(1'b1),
    .pin9(1'b1), .pin12(1'b1), .pin13(1'b1), .pin14(1'b1));  // open: pin4, pin10, pin11
  LED NAND (.in(_7400_1_pin3));
  LED NOR (.in(_7402_1_pin1));
  LED XNOR (.in(_747266_1_pin3));
endmodule
