// Digital circuit adv-BUFFERS.dig as structural Verilog
module adv_BUFFERS (
);

  wire _7404_1_pin1, polarityawareled_1_p2, polarityawareled_2_p1, pullup_1_out, pullup_2_out, pullup_3_out,
       switchdt_1_p1, switchdt_1_p3;

  PullUp pullup_1 (.out(pullup_1_out));
  PullUp pullup_2 (.out(pullup_2_out));
  // PolarityAwareLED polarityawareled_1: pin names not known; wires that end beside it: pullup_2_out, polarityawareled_1_p2
  // PolarityAwareLED polarityawareled_2: pin names not known; wires that end beside it: polarityawareled_2_p1, pullup_1_out
  _7404 _7404_1 (
    .pin1(_7404_1_pin1), .pin2(polarityawareled_1_p2), .pin3(_7404_1_pin1), .pin5(_7404_1_pin1), .pin7(1'b0),
    .pin9(_7404_1_pin1), .pin11(_7404_1_pin1), .pin13(_7404_1_pin1), .pin14(1'b1));  // open: pin4, pin6, pin8, pin10, pin12
  _7407 _7407_1 (
    .pin1(_7404_1_pin1), .pin2(polarityawareled_2_p1), .pin3(_7404_1_pin1), .pin5(_7404_1_pin1), .pin7(1'b0),
    .pin9(_7404_1_pin1), .pin11(_7404_1_pin1), .pin13(_7404_1_pin1), .pin14(1'b1));  // open: pin4, pin6, pin8, pin10, pin12
  // SwitchDT switchdt_1: pin names not known; wires that end beside it: switchdt_1_p1, 1'b0, switchdt_1_p3
  PullUp pullup_3 (.out(pullup_3_out));
  // PolarityAwareLED polarityawareled_3: pin names not known; wires that end beside it: _7404_1_pin1, pullup_3_out
  _7408 _7408_1 (
    .pin1(switchdt_1_p1), .pin2(switchdt_1_p3), .pin3(_7404_1_pin1), .pin4(1'b0), .pin5(1'b0), .pin7(1'b0),
    .pin9(1'b0), .pin10(1'b0), .pin12(1'b0), .pin13(1'b0), .pin14(switchdt_1_p1));  // open: pin6, pin8, pin11
  PullUp pullup_4 (.out(switchdt_1_p1));
endmodule
