// Digital circuit adv-NAND.dig as structural Verilog
module adv_NAND (
  input  A,
  input  B
);

  wire nand_1_out, nand_2_out, nand_3_out, nand_4_out, nand_5_out, nand_6_out, nand_7_out, nand_8_out,
       nand_9_out, nand_10_out, nand_11_out, nand_12_out, nand_13_out, nand_14_out, nand_16_out, nand_17_out,
       nand_18_out, nand_19_out, nand_20_out, nand_21_out, nand_22_out;

  nand nand_1 (nand_1_out, A, A);
  nand nand_2 (nand_2_out, B, B);
  nand nand_3 (nand_3_out, A, B);
  nand nand_4 (nand_4_out, A, A);
  nand nand_5 (nand_5_out, B, B);
  nand nand_6 (nand_6_out, A, B);
  nand nand_7 (nand_7_out, A, B);
  nand nand_8 (nand_8_out, A, A);
  nand nand_9 (nand_9_out, B, B);
  nand nand_10 (nand_10_out, A, B);
  LED NOT_A (.in(nand_1_out));
  LED NOT_B (.in(nand_2_out));
  nand nand_11 (nand_11_out, nand_3_out, nand_3_out);
  nand nand_12 (nand_12_out, nand_4_out, nand_5_out);
  nand nand_13 (nand_13_out, A, nand_6_out);
  nand nand_14 (nand_14_out, nand_6_out, B);
  LED NAND_15 (.in(nand_7_out));
  nand nand_16 (nand_16_out, nand_8_out, nand_9_out);
  nand nand_17 (nand_17_out, A, nand_10_out);
  nand nand_18 (nand_18_out, nand_10_out, B);
  LED AND (.in(nand_11_out));
  LED OR (.in(nand_12_out));
  nand nand_19 (nand_19_out, nand_13_out, nand_14_out);
  nand nand_20 (nand_20_out, nand_16_out, nand_16_out);
  nand nand_21 (nand_21_out, nand_17_out, nand_18_out);
  LED XOR (.in(nand_19_out));
  LED NOR (.in(nand_20_out));
  nand nand_22 (nand_22_out, nand_21_out, nand_21_out);
  LED XNOR (.in(nand_22_out));
endmodule
