// Digital circuit adv-SWITCH.dig as structural Verilog
module adv_SWITCH (
);

  wire polarityawareled_1_p1, polarityawareled_1_p2, switchdt_1_p1, switchdt_1_p3;

  // SwitchDT switchdt_1: pin names not known; wires that end beside it: switchdt_1_p1, 1'b0, switchdt_1_p3
  // PolarityAwareLED polarityawareled_1: pin names not known; wires that end beside it: polarityawareled_1_p1, polarityawareled_1_p2
  PullDown pulldown_1 (.out(polarityawareled_1_p2));
  _7408 _7408_1 (
    .pin1(switchdt_1_p1), .pin2(switchdt_1_p3), .pin3(polarityawareled_1_p1), .pin4(1'b0), .pin5(1'b0),
    .pin7(1'b0), .pin9(1'b0), .pin10(1'b0), .pin12(1'b0), .pin13(1'b0), .pin14(switchdt_1_p1));  // open: pin6, pin8, pin11
  PullUp pullup_1 (.out(switchdt_1_p1));
endmodule
